# Fritzing sketch timbangan digital (saved by Fritzing 0.9.3b)

parts:
  Part1 = Arduino Uno (Rev3)
  Part2 = Bluetooth HC-05 Macho
  Part3 = SRF05 Ultrasonic Rangefinder
  Part4 = HX711 Weighing Sensor Module
  Load_Cell1 = Load Cell - Red/white/black/green
  LCD2004-I2C1 = LCD2004-I2C

nets:
  N1: Part1.D8, Part3.Echo
  N2: Part1.D9_PWM, Part3.Trig
  GND: Part1.GND, Part2.GND, Part3.GND, Part4.GND, LCD2004-I2C1.GND
  N3: Part1.D0/RX, Part2.TXD, Part4.DO/RX
  N4: Part1.D1/TX, Part2.RXD, Part4.CK/TX
  VCC: Part1.5V, Part2.VCC, Part3.VCC, Part4.VCC, LCD2004-I2C1.VCC
  N5: Part4.E+, Load_Cell1.wire1
  N6: Part4.E-, Load_Cell1.wire2
  N7: Part4.A+, Load_Cell1.wire3
  N8: Part4.A-, Load_Cell1.wire4

custom parts:
  Load Cell - Red/white/black/green: A rectangle load cell/weighting pressure Sensor with four wires - Red, white, black, green. Normally corresponding with E+, E-, A+, A- respectively.
  LCD2004-I2C: A standard character display with 4x20 characters. Comes in many colors with LCM2004 IIC attached.
